# Fritzing sketch Mega328p-w_ISPLayout (saved by Fritzing 0.9.3b)
breadboards: 1

parts:
  U1 = atmega328 [package=dip]
  XTAL1 = Crystal [frequency="16 Mhz" package=THT]
  C1 = Ceramic Capacitor [capacitance=100nF package="100 mil [THT, multilayer]"]
  C2 = Ceramic Capacitor [capacitance=100nF package="100 mil [THT, multilayer]"]

nets:
  N1: U1.GND#7, C1.1, C2.0
  N2: U1.XLAT1, XTAL1.pin_0, C2.1
  N3: U1.XLAT2, XTAL1.pin_1, C1.0
